# Fritzing sketch obstacle-avoidance (saved by Fritzing 0.9.3b)
breadboards: 1

parts:
  Raspberry_Pi1 = Raspberry Pi B rev2
  J1 = Infrared Proximity Sensor

nets:
  3V3: Raspberry_Pi1.3V3, J1.Vcc
  GND: Raspberry_Pi1.GND, J1.GND
  N1: Raspberry_Pi1.GPIO_18, J1.Vout

notes:
  Obstacle Avoidance Sensor
