# Fritzing sketch vibration (saved by Fritzing 0.9.3b)
breadboards: 1

parts:
  Raspberry_Pi1 = Raspberry Pi B rev2
  U1 = TMP36 [package=to-92-kit]
  LED1 = smd LED [color="Red (633nm)" package="0805 [SMD]"]
  R1 = Resistor [tolerance=±5% resistance=220 package="2010 [SMD]"]
  R2 = Resistor [tolerance=±5% resistance=220 package="2010 [SMD]"]

nets:
  N1: Raspberry_Pi1.3V3, R1.Pin_1
  N2: Raspberry_Pi1.GPIO_17, LED1.cathode
  N3: Raspberry_Pi1.GPIO_18, U1.VOUT
  N4: U1.VCC, R1.Pin_0
  N5: U1.GND, R2.Pin_1
  N6: LED1.anode, R2.Pin_0
